// Logisim project ControlUnit.circ as structural Verilog: 1 circuit, main circuit Control Unit
module Control_Unit (
  input  [9:0] in_1,
  output [9:0] out_2
);

  wire clock_1_out;

  Clock clock_1 (.out(clock_1_out));
  _10BitRegister PC (.clk(1'b1), .W_Enable(clock_1_out), .I(in_1), .Q(out_2));
  _10BitIncrementer u_10bitincrementer_1 (.I(out_2), .O(in_1));

  // Notes on the sheet:
  //   out_2: pull=down
  //   in_1: pull=down
endmodule
